# Fritzing sketch IOT_Thinkspeak_Spring2018 (saved by Fritzing 0.9.4)
breadboards: 2

parts:
  Adafruit_Huzza_ESP8266 = Adafruit Feather HUZZAH ESP8266 [part_number="Adafruit #2821"]
  Adafruit_BME280 = Adafruit BME280
  DS3231 = Adafruit DS3231 [part_number="Adafruit #3013"]
  Adafruit_2_8"_TFT_LCD = TFT 2.2 inch 320x240 w microSD [part_number=1480]
  SWITCH = Toggle Switch [package=THT]
  AC/DC_9V_Power_Adapter = Power plug

nets:
  N1: Adafruit_Huzza_ESP8266.GPIO12/MISO, Adafruit_2_8"_TFT_LCD.MISO
  N2: Adafruit_Huzza_ESP8266.GPIO13/MOSI, Adafruit_2_8"_TFT_LCD.MOSI
  N3: Adafruit_Huzza_ESP8266.GPIO14/SCK, Adafruit_2_8"_TFT_LCD.SCLK
  GND: Adafruit_Huzza_ESP8266.GND, Adafruit_BME280.GND, DS3231.GND, Adafruit_2_8"_TFT_LCD.GND, AC/DC_9V_Power_Adapter.GND
  N4: Adafruit_Huzza_ESP8266.GPIO0, Adafruit_2_8"_TFT_LCD.LCDCS
  N5: Adafruit_Huzza_ESP8266.GPIO5/SCL, Adafruit_BME280.SCK/SCL, DS3231.SCL
  N6: Adafruit_Huzza_ESP8266.GPIO4/SDA, Adafruit_BME280.SDO/ADR, DS3231.SDA
  VIN: Adafruit_BME280.VIN, DS3231.Vin, Adafruit_2_8"_TFT_LCD.VIN
  N7: SWITCH.COM, AC/DC_9V_Power_Adapter.VCC

notes:
  3.3V/800mA max
  TFT IM1 IM2 IM3 PINS NEED TO CONNECT TO 3Vo PIN
  I2C BUS SCL(YELLOW) SDA(BLUE)
  SPI BUS SCK(GREEN) MISO(PURPLE) MOSI(GREY) LCD CS(CYAN)
  ESP8266 POWER OPTIONS
  MICRO USB CABLE OR
  4.2/3.7 LIPO OR LILON BATTERY TO JST

custom parts:
  Adafruit Feather HUZZAH ESP8266: his is the Adafruit Feather HUZZAH ESP8266 - our take on an 'all-in-one' ESP8266 WiFi development board with built in USB and battery charging. Its an ESP8266 WiFi module with all the extras you need, ready to rock! We have other boards in the Feather family, check'em out here. At the Feather HUZZAH's heart is an ESP8266 WiFi microcontroller clocked at 80 MHz and at 3.3V logic. This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
  Adafruit BME280: Bosch has stepped up their game with their new BME280 sensor, an environmental sensor with temperature, barometric pressure and humidity! This sensor is great for all sorts of weather/environmental sensing and can even be used in both I2C and SPI! This precision sensor from Bosch is the best low-cost sensing solution for measuring humidity with ±3% accuracy, barometric pressure with ±1 hPa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
  Adafruit DS3231: The datasheet for the DS3231 explains that this part is an "Extremely Accurate I²C-Integrated RTC/TCXO/Crystal". And, hey, it does exactly what it says on the tin! This Real Time Clock (RTC) is the most precise you can get in a small, low power package. Most RTCs use an external 32kHz timing crystal that is used to keep time with low current draw. And that's all well and good, but those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
  TFT 2.2 inch 320x240 w microSD: This lovely little display breakout is the best way to add a small, colorful and bright display to any project. Since the display uses 4-wire SPI to communicate and has its own pixel-addressable frame buffer, it can be used with every kind of microcontroller. Even a very small one with low memory and few pins available! The 2.2" display has 320x240 color pixels.
