# Fritzing sketch IOT_Thinkspeak_Spring2018 (saved by Fritzing 0.9.4)
circuit board: 20.403cm x 9.93771cm
breadboards: 1

parts:
  Adafruit_Huzza_ESP8266 = Adafruit Feather HUZZAH ESP8266 [part_number="Adafruit #2821"]
  Adafruit_BME280 = Adafruit BME280
  DS3231 = Adafruit DS3231 [part_number="Adafruit #3013"]
  Part1 = Adafruit 2.8 inch Captouch TFT [part_number="Adafruit #2090"]
  S1 = Toggle Switch [package=THT]
  R2 = 1K Ω Resistor [package=THT]
  C3_100nF1 = Capacitor [package=cap-pth-small2]
  C4_1nF1 = Capacitor [package=cap-pth-small2]
  C2_100uF_35V1 = Electrolytic Capacitor [capacitance=100μF package="200 mil [THT, electrolytic]"]
  C1_470uF_25V1 = Electrolytic Capacitor [capacitance=100µF package="200 mil [THT, electrolytic]"]
  Power_plug_9V/1AMP = Power plug
  D1 = Rectifier Diode [part_number=1N4005 package="300 mil [THT]"]
  LED1 = LED - 5mm [color="Red (633nm)" package="5 mm [THT]"]
  U1 = V_REG_LD1117V33 [package=78xxl]

nets:
  N1: Adafruit_Huzza_ESP8266.GPIO12/MISO, Part1.MISO
  N2: Adafruit_Huzza_ESP8266.GPIO13/MOSI, Part1.MOSI
  N3: Adafruit_Huzza_ESP8266.GPIO14/SCK, Part1.C/D_CLK
  GND: Adafruit_Huzza_ESP8266.GND, Adafruit_BME280.GND, DS3231.GND, Part1.GND, R2.Pin_0, C3_100nF1.C4#1, C4_1nF1.C4#1, C2_100uF_35V1.-, C1_470uF_25V1.-, Power_plug_9V/1AMP.GND, LED1.cathode, U1.Vout
  N4: Adafruit_Huzza_ESP8266.GPIO0, Part1.CS
  N5: Adafruit_Huzza_ESP8266.GPIO5/SCL, Adafruit_BME280.SCK/SCL, DS3231.SCL
  N6: Adafruit_Huzza_ESP8266.GPIO4/SDA, Adafruit_BME280.SDI/SDA, DS3231.SDA
  VIN: Adafruit_BME280.VIN, DS3231.Vin, Part1.VIN, R2.Pin_1, C4_1nF1.C4#0, C2_100uF_35V1.+, LED1.anode, U1.GND
  N7: Part1.3.3V, Part1.IM3, Part1.IM2, Part1.IM1
  N8: S1.L1, D1.anode
  N9: S1.COM, Power_plug_9V/1AMP.VCC
  N10: C3_100nF1.C4#0, C1_470uF_25V1.+, D1.cathode, U1.Vin

notes:
  3.3V/800mA max
  TFT IM1 IM2 IM3 PINS NEED TO CONNECT TO 3Vo PIN
  I2C BUS SCL(YELLOW) SDA(BLUE)
  SPI BUS SCK(GREEN) MISO(PURPLE) MOSI(GREY) LCD CS(CYAN)
  ESP8266 POWER OPTIONS
  MICRO USB CABLE OR
  4.2/3.7 LIPO OR LILON BATTERY TO JST
  Voltage Regulator LD1117V33 3.3V/800mA Max

custom parts:
  Adafruit Feather HUZZAH ESP8266: his is the Adafruit Feather HUZZAH ESP8266 - our take on an 'all-in-one' ESP8266 WiFi development board with built in USB and battery charging. Its an ESP8266 WiFi module with all the extras you need, ready to rock! We have other boards in the Feather family, check'em out here. At the Feather HUZZAH's heart is an ESP8266 WiFi microcontroller clocked at 80 MHz and at 3.3V logic. This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
  Adafruit BME280: Bosch has stepped up their game with their new BME280 sensor, an environmental sensor with temperature, barometric pressure and humidity! This sensor is great for all sorts of weather/environmental sensing and can even be used in both I2C and SPI! This precision sensor from Bosch is the best low-cost sensing solution for measuring humidity with ±3% accuracy, barometric pressure with ±1 hPa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
  Adafruit DS3231: The datasheet for the DS3231 explains that this part is an "Extremely Accurate I²C-Integrated RTC/TCXO/Crystal". And, hey, it does exactly what it says on the tin! This Real Time Clock (RTC) is the most precise you can get in a small, low power package. Most RTCs use an external 32kHz timing crystal that is used to keep time with low current draw. And that's all well and good, but those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
  Adafruit 2.8 inch Captouch TFT: Add some jazz & pizazz to your project with a color capactive touchscreen LCD. This TFT display is big (2.8" diagonal) bright (4 white-LED backlight) and colorful! 240x320 pixels with individual RGB pixel control, this has way more resolution than a black and white 128x64 display. As a bonus, this display has a capacitive single-touch touchscreen attached to it already, so you can detect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
  1K Ω Resistor: A generic resistor (0.25W)
  Capacitor: Capacitor Standard 0603 ceramic capacitor, and 0.1 leaded capacitor.
  Rectifier Diode: A standard rectifier diode
  V_REG_LD1117V33: LD1117VXX voltage regulator. We carry the 3.3V version (COM-00526) in TO-220 package.
